// Logisim project cpu.circ as structural Verilog: 6 circuits, main circuit main
module main (
);

  wire and_1_out, and_2_out, and_3_out, and_4_out, and_5_out, and_6_out, and_7_out, and_8_out, and_9_out,
       and_10_out, and_11_out, and_12_out, and_13_out, and_14_out, and_15_out, and_16_out, and_17_out,
       and_18_out, and_19_out, and_20_out, and_21_out, and_22_out, and_23_out, and_24_out, and_25_out,
       and_26_out, and_27_out, and_28_out, and_29_out, and_30_out, clock_1_out, clock_2_out, comparator_1_lt,
       comparator_2_lt, comparator_3_eq, comparator_3_gt, comparator_3_lt, counter_2_q, counter_3_carry,
       counter_4_q, counter_5_carry, counter_5_q, cu_1_condition_met, decoder_1_out0, decoder_1_out1,
       decoder_1_out2, decoder_1_out3, decoder_1_out4, decoder_2_out0, decoder_2_out1, decoder_2_out2,
       decoder_2_out3, decoder_2_out4, decoder_2_out5, decoder_2_out6, decoder_2_out7, decoder_3_out0,
       decoder_3_out1, decoder_3_out2, decoder_3_out3, decoder_3_out5, decoder_3_out6, decoder_3_out7,
       multiplexer_1_out, not_1_out, or_1_out, or_2_out, or_3_out, or_4_out, or_5_out, or_6_out, or_7_out,
       or_8_out, or_9_out;
  wire [2:0] bitselector_1_out, bitselector_2_out, bitselector_3_out;
  wire [6:0] keyboard_1_data;
  wire [7:0] wtb_1_out_2, wtb_2_out_2, wtb_3_out_2, wtb_4_out_2, wtb_5_out_2;
  wire [15:0] alu_1_result, controlled_buffer_1_out, controlled_buffer_2_out, controlled_buffer_7_out,
       counter_1_q, pull_resistor_1_node, pull_resistor_2_node, ram_1_dout, register_1_q, register_2_q,
       register_3_q, register_4_q, register_5_q, register_6_q, register_7_q, register_8_q, register_9_q,
       register_10_q, register_11_q, shift_register_1_out, shift_register_1_q0, shift_register_1_q1,
       shift_register_1_q2, shift_register_1_q3;
  wire [23:0] rgbc_1_out_4;
  wire [47:0] rom_1_data;

  ROM #(.addrWidth(16), .dataWidth(48)) rom_1 (.addr(counter_1_q), .data(rom_1_data));
  Clock #(.highDuration(2), .lowDuration(2)) clock_1 (.out(clock_1_out));
  or or_1 (or_1_out, and_1_out, clock_1_out);
  Counter #(.max('hffff), .width(16)) counter_1 (
    .load(and_1_out), .D(rom_1_data[31:16]), .count(not_1_out), .Q(counter_1_q), .up(1'b1), .clk(or_1_out));  // open: carry, clr
  not not_1 (not_1_out, and_1_out);
  and and_1 (and_1_out, and_2_out, clock_1_out);
  and and_2 (and_2_out, cu_1_condition_met, clock_2_out, decoder_1_out3);
  BitSelector #(.group(3), .width(16)) bitselector_1 (.in(rom_1_data[47:32]), .out(bitselector_1_out), .sel(3'b000));
  Decoder #(.select(3)) decoder_1 (
    .out0(decoder_1_out0), .out1(decoder_1_out1), .out2(decoder_1_out2), .out3(decoder_1_out3),
    .out4(decoder_1_out4), .sel(bitselector_1_out), .en(1'b1));  // open: out5, out6, out7
  Clock clock_2 (.out(clock_2_out));
  and and_3 (and_3_out, ~clock_2_out, decoder_1_out4, clock_1_out);  // AND_Gate
  and and_4 (and_4_out, clock_2_out, decoder_1_out4, clock_1_out);
  and and_5 (and_5_out, ~clock_2_out, decoder_1_out4, ~clock_1_out);  // AND_Gate
  Register #(.trigger("high"), .width(16)) register_1 (
    .D(pull_resistor_1_node), .Q(register_1_q), .clk(and_3_out));  // open: en, clr
  assign controlled_buffer_1_out = and_5_out ? register_2_q : 16'bz;  // Controlled_Buffer controlled_buffer_1
  Register #(.trigger("high"), .width(16)) register_2 (
    .D(pull_resistor_1_node), .Q(register_2_q), .clk(and_4_out));  // open: en, clr
  assign controlled_buffer_2_out = and_5_out ? rom_1_data[15:0] : 16'bz;  // Controlled_Buffer controlled_buffer_2
  and and_6 (and_6_out, ~1'b0, decoder_1_out0, clock_1_out);  // AND_Gate
  and and_7 (and_7_out, clock_2_out, or_4_out, clock_1_out);
  and and_8 (and_8_out, ~1'b0, or_4_out, clock_1_out);  // AND_Gate
  and and_9 (and_9_out, and_7_out, comparator_2_lt);
  and and_10 (and_10_out, comparator_2_lt, and_5_out);
  or or_2 (or_2_out, decoder_1_out1, decoder_1_out0, and_3_out);
  assign controlled_buffer_2_out = and_4_out ? register_1_q : 16'bz;  // Controlled_Buffer controlled_buffer_3
  and and_11 (and_11_out, and_5_out, ~comparator_2_lt);  // AND_Gate
  assign controlled_buffer_2_out = or_2_out ? rom_1_data[31:16] : 16'bz;  // Controlled_Buffer controlled_buffer_4
  assign controlled_buffer_2_out = and_13_out ? rom_1_data[31:16] : 16'bz;  // Controlled_Buffer controlled_buffer_5
  assign controlled_buffer_2_out = and_12_out ? rom_1_data[31:16] : 16'bz;  // Controlled_Buffer controlled_buffer_6
  or or_3 (or_3_out, and_9_out, and_10_out);
  or or_4 (or_4_out, decoder_1_out1, decoder_1_out0);
  and and_12 (and_12_out, clock_2_out, decoder_1_out2);
  and and_13 (and_13_out, ~clock_2_out, decoder_1_out2);  // AND_Gate
  Comparator #(.mode("unsigned"), .width(16)) comparator_1 (
    .a(controlled_buffer_2_out), .b(16'h9), .lt(comparator_1_lt));  // open: gt, eq
  BitSelector #(.group(3), .width(16)) bitselector_2 (
    .in(controlled_buffer_2_out), .out(bitselector_2_out), .sel(3'b000));
  Decoder #(.select(3)) decoder_2 (
    .out0(decoder_2_out0), .out1(decoder_2_out1), .out2(decoder_2_out2), .out3(decoder_2_out3),
    .out4(decoder_2_out4), .out5(decoder_2_out5), .out6(decoder_2_out6), .out7(decoder_2_out7),
    .sel(bitselector_2_out), .en(1'b1));
  BitSelector #(.group(3), .width(16)) bitselector_3 (.in(rom_1_data[15:0]), .out(bitselector_3_out), .sel(3'b000));
  Decoder #(.select(3)) decoder_3 (
    .out0(decoder_3_out0), .out1(decoder_3_out1), .out2(decoder_3_out2), .out3(decoder_3_out3),
    .out5(decoder_3_out5), .out6(decoder_3_out6), .out7(decoder_3_out7), .sel(bitselector_3_out),
    .en(or_3_out));  // open: out4
  Comparator #(.mode("unsigned"), .width(16)) comparator_2 (
    .a(rom_1_data[15:0]), .b(16'h9), .lt(comparator_2_lt));  // open: gt, eq
  Register #(.width(16)) register_3 (.D(pull_resistor_1_node), .Q(register_3_q), .clk(and_12_out));  // open: en, clr
  Comparator #(.width(16)) comparator_3 (
    .a(register_3_q), .b(register_4_q), .gt(comparator_3_gt), .eq(comparator_3_eq), .lt(comparator_3_lt));
  Register #(.width(16)) register_4 (.D(pull_resistor_1_node), .Q(register_4_q), .clk(and_13_out));  // open: en, clr
  and and_14 (and_14_out, decoder_1_out0, and_6_out, comparator_1_lt);
  and and_15 (and_15_out, ~comparator_2_lt, and_7_out, or_4_out);  // AND_Gate
  CU cu_1 (
    .CONDITION(rom_1_data[15:0]), .GT(comparator_3_gt), .EQ(comparator_3_eq), .LT(comparator_3_lt),
    .CONDITION_MET(cu_1_condition_met));
  and and_16 (and_16_out, and_6_out, ~and_14_out);  // AND_Gate
  Multiplexer multiplexer_1 (.in0(comparator_2_lt), .in1(comparator_1_lt), .out(multiplexer_1_out), .sel(and_13_out));
  and and_17 (and_17_out, ~comparator_1_lt, and_4_out);  // AND_Gate
  and and_18 (and_18_out, comparator_1_lt, and_4_out);
  and and_19 (and_19_out, decoder_1_out2, multiplexer_1_out);
  or or_5 (or_5_out, and_22_out, and_21_out);
  assign controlled_buffer_7_out = and_7_out ? rom_1_data[15:0] : 16'bz;  // Controlled_Buffer controlled_buffer_7
  assign controlled_buffer_7_out = and_20_out ? controlled_buffer_2_out : 16'bz;  // Controlled_Buffer controlled_buffer_8
  assign controlled_buffer_7_out = and_11_out ? rom_1_data[15:0] : 16'bz;  // Controlled_Buffer controlled_buffer_9
  or or_6 (or_6_out, and_3_out, and_14_out, and_19_out);
  and and_20 (and_20_out, and_6_out, ~and_7_out);  // AND_Gate
  assign controlled_buffer_7_out = and_21_out ? controlled_buffer_2_out : 16'bz;  // Controlled_Buffer controlled_buffer_10
  assign controlled_buffer_7_out = and_22_out ? controlled_buffer_2_out : 16'bz;  // Controlled_Buffer controlled_buffer_11
  or or_7 (or_7_out, and_18_out, or_6_out);
  and and_21 (and_21_out, clock_2_out, decoder_1_out2, ~comparator_2_lt);  // AND_Gate
  or or_8 (or_8_out, and_15_out, and_11_out);
  Pull_Resistor #(.pull(1)) pull_resistor_1 (.node(pull_resistor_1_node));
  Register #(.width(16)) register_5 (
    .D(pull_resistor_2_node), .Q(register_5_q), .clk(decoder_3_out0));  // open: en, clr
  Register #(.width(16)) register_6 (
    .D(pull_resistor_2_node), .Q(register_6_q), .clk(decoder_3_out1));  // open: en, clr
  Register #(.width(16)) register_7 (
    .D(pull_resistor_2_node), .Q(register_7_q), .clk(decoder_3_out2));  // open: en, clr
  Register #(.width(16)) register_8 (
    .D(pull_resistor_2_node), .Q(register_8_q), .clk(decoder_3_out3));  // open: en, clr
  Register #(.width(16)) register_9 (
    .D(pull_resistor_2_node), .Q(register_9_q), .clk(decoder_3_out6));  // open: en, clr
  and and_22 (and_22_out, ~clock_2_out, decoder_1_out2, ~comparator_1_lt);  // AND_Gate
  Register #(.width(16)) register_10 (
    .D(pull_resistor_2_node), .Q(register_10_q), .clk(decoder_3_out7));  // open: en, clr
  RAM #(.addrWidth(16), .dataWidth(16), .enables("line"), .\type ("nonvolatile")) ram_1 (
    .addr(controlled_buffer_7_out), .we(counter_2_q), .clk(counter_2_q), .din(pull_resistor_2_node),
    .dout(ram_1_dout));
  Counter #(.max('h1), .width(1)) counter_2 (.Q(counter_2_q), .clk(or_8_out));  // open: load, D, count, carry, up, clr
  Pull_Resistor #(.pull(1)) pull_resistor_2 (.node(pull_resistor_2_node));
  and and_23 (and_23_out, decoder_2_out0, or_7_out);
  assign pull_resistor_1_node = and_23_out ? register_5_q : 16'bz;  // Controlled_Buffer controlled_buffer_12
  and and_24 (and_24_out, decoder_2_out1, or_7_out);
  assign pull_resistor_1_node = and_24_out ? register_6_q : 16'bz;  // Controlled_Buffer controlled_buffer_13
  and and_25 (and_25_out, decoder_2_out2, or_7_out);
  assign pull_resistor_1_node = and_25_out ? register_7_q : 16'bz;  // Controlled_Buffer controlled_buffer_14
  and and_26 (and_26_out, decoder_2_out3, or_7_out);
  assign pull_resistor_1_node = and_26_out ? register_8_q : 16'bz;  // Controlled_Buffer controlled_buffer_15
  and and_27 (and_27_out, decoder_2_out4, or_7_out);
  assign pull_resistor_1_node = and_27_out ? alu_1_result : 16'bz;  // Controlled_Buffer controlled_buffer_16
  and and_28 (and_28_out, decoder_2_out5, or_7_out);
  assign pull_resistor_1_node = and_28_out ? {{9{1'b0}}, keyboard_1_data} : 16'bz;  // Controlled_Buffer controlled_buffer_17
  and and_29 (and_29_out, decoder_2_out6, or_7_out);
  assign pull_resistor_1_node = and_29_out ? register_9_q : 16'bz;  // Controlled_Buffer controlled_buffer_18
  and and_30 (and_30_out, decoder_2_out7, or_7_out);
  assign pull_resistor_1_node = and_30_out ? register_10_q : 16'bz;  // Controlled_Buffer controlled_buffer_19
  or or_9 (or_9_out, or_5_out, and_17_out, and_16_out);
  ALU alu_1 (.Instruction(register_6_q), .A(register_7_q), .B(register_8_q), .CLK(clock_2_out), .Result(alu_1_result));
  assign pull_resistor_1_node = decoder_1_out1 ? controlled_buffer_2_out : 16'bz;  // Controlled_Buffer controlled_buffer_20
  assign pull_resistor_1_node = or_9_out ? ram_1_dout : 16'bz;  // Controlled_Buffer controlled_buffer_21
  Counter #(.max('h5)) counter_3 (
    .carry(counter_3_carry), .up(1'b1), .clk(decoder_3_out6), .clr(counter_3_carry));  // open: load, D, count, Q
  Counter #(.max('h1), .width(1)) counter_4 (
    .Q(counter_4_q), .clk(and_28_out));  // open: load, D, count, carry, up, clr
  Register #(.trigger("high"), .width(16)) register_11 (
    .D(pull_resistor_1_node), .Q(register_11_q), .clk(and_8_out));  // open: en, clr
  Multiplexer #(.width(16)) multiplexer_2 (
    .in0(register_11_q), .in1(controlled_buffer_1_out), .out(pull_resistor_2_node), .sel(and_5_out));
  // Probe on shift_register_1_q0
  // Probe on shift_register_1_q1
  // Probe on shift_register_1_q2
  // Probe on shift_register_1_q3
  // Probe on shift_register_1_out
  Counter #(.max('h1), .width(1)) counter_5 (
    .Q(counter_5_q), .carry(counter_5_carry), .clk(counter_3_carry), .clr(counter_5_carry));  // open: load, D, count, up
  Shift_Register #(.length(5), .width(16)) shift_register_1 (
    .in(pull_resistor_2_node), .clk(decoder_3_out6), .out(shift_register_1_out), .q0(shift_register_1_q0),
    .q1(shift_register_1_q1), .q2(shift_register_1_q2), .q3(shift_register_1_q3));  // open: shift, load, clr, d0, d1, d2, d3, d4, q4
  WtB wtb_1 (.in_1(shift_register_1_out), .out_2(wtb_1_out_2));
  WtB wtb_2 (.in_1(shift_register_1_q3), .out_2(wtb_2_out_2));
  WtB wtb_3 (.in_1(shift_register_1_q2), .out_2(wtb_3_out_2));
  WtB wtb_4 (.in_1(shift_register_1_q1), .out_2(wtb_4_out_2));
  WtB wtb_5 (.in_1(shift_register_1_q0), .out_2(wtb_5_out_2));
  RGBC rgbc_1 (.in_1(wtb_3_out_2), .in_2(wtb_4_out_2), .in_3(wtb_5_out_2), .out_4(rgbc_1_out_4));
  TTY tty_1 (.data(pull_resistor_2_node[6:0]), .clk(decoder_3_out7));  // open: we, clr
  Keyboard #(.trigger("falling")) keyboard_1 (.clk(counter_4_q), .data(keyboard_1_data));  // open: re, clr, avail
  // RGB_Video #(.cursor("No Cursor"), .height(256), .scale(1), .width(256)) rgb_video_1: pin names not known; wires that end beside it: counter_5_q, counter_5_q, wtb_1_out_2, wtb_2_out_2, rgbc_1_out_4

  // Notes on the sheet:
  //   contents of rom_1 (hex, n*v repeats v):
  //   0 100480007 100650007 1006c0007 1006c0007 1006f0007 1002c0007 100200007 100770007 100680007
  //   100610007 100740007 100270007 100730007 100200007 100790007 1006f0007 100750007 100720007 100200007
  //   1006e0007 100610007 1006d0007 100650007 100200007 1003f0007 1000a0007 1003e0007 100200007 0
  //   1000a0101 0 50000 7 201010000 300250001 3001f0000 0 300250000
endmodule

// Arithmetic & Logic Unit
module ALU (
  input  [15:0] Instruction,
  input  [15:0] A,
  input  [15:0] B,
  input  CLK,
  output [15:0] Result
);

  wire [15:0] adder_1_out, and_1_out, divider_1_out, divider_1_rem, multiplier_1_out, nand_1_out, nor_1_out,
       or_1_out, shifter_1_out, shifter_2_out, shifter_3_out, shifter_4_out, subtractor_1_out, undriven,
       xnor_1_out, xor_1_out;

  Adder #(.width(16)) adder_1 (.a(A), .b(B), .out(adder_1_out));  // open: cin, cout
  Divider #(.width(16)) divider_1 (.a(A), .b(B), .out(divider_1_out), .rem(divider_1_rem));  // open: upper
  Subtractor #(.width(16)) subtractor_1 (.a(A), .b(B), .out(subtractor_1_out));  // open: bin, bout
  Multiplier #(.width(16)) multiplier_1 (.a(A), .b(B), .out(multiplier_1_out));  // open: cin, cout
  assign and_1_out = A & B;  // AND_Gate and_1, 16 bits wide
  assign or_1_out = A | B;  // OR_Gate or_1, 16 bits wide
  assign xor_1_out = A ^ B;  // XOR_Gate xor_1, 16 bits wide
  assign nand_1_out = ~(A & B);  // NAND_Gate nand_1, 16 bits wide
  assign nor_1_out = ~(A | B);  // NOR_Gate nor_1, 16 bits wide
  assign xnor_1_out = ~(A ^ B);  // XNOR_Gate xnor_1, 16 bits wide
  Shifter #(.width(16)) shifter_1 (.in(A), .\dist (B[3:0]), .out(shifter_1_out));
  Shifter #(.shift("lr"), .width(16)) shifter_2 (.in(A), .\dist (B[3:0]), .out(shifter_2_out));
  Shifter #(.shift("rl"), .width(16)) shifter_3 (.in(A), .\dist (B[3:0]), .out(shifter_3_out));
  Shifter #(.shift("rr"), .width(16)) shifter_4 (.in(A), .\dist (B[3:0]), .out(shifter_4_out));
  // Random #(.width(16)) random_1: pin names not known; wires that end beside it: CLK, CLK
  Multiplexer #(.select(5), .width(16)) multiplexer_1 (
    .in0(adder_1_out), .in1(divider_1_out), .in2(divider_1_rem), .in3(subtractor_1_out),
    .in4(multiplier_1_out), .in5(and_1_out), .in6(or_1_out), .in7(xor_1_out), .in8(nand_1_out),
    .in9(nor_1_out), .in10(xnor_1_out), .in11(shifter_1_out), .in12(shifter_2_out), .in13(shifter_3_out),
    .in14(shifter_4_out), .in15(undriven), .out(Result), .sel(Instruction[4:0]));  // open: in16, in17, in18, in19, in20, in21, in22, in23, in24, in25, in26, in27, in28, in29, in30, in31
endmodule

module TSwitch (
  input  in_1,
  input  in_2,
  output out_3
);

  wire not_1_out;

  not not_1 (not_1_out, in_1);
  Transistor transistor_1 (.in(in_2), .out(out_3), .gate(not_1_out));
endmodule

// Conditionnal Unit
module CU (
  input  [15:0] CONDITION,
  input  GT,
  input  EQ,
  input  LT,
  output CONDITION_MET
);

  wire and_1_out, and_2_out, and_3_out, and_4_out, and_5_out, and_6_out, decoder_1_out0, decoder_1_out1,
       decoder_1_out2, decoder_1_out3, decoder_1_out4, decoder_1_out5, decoder_1_out6, not_1_out, or_1_out,
       or_2_out;

  Decoder #(.enable("false"), .select(5)) decoder_1 (
    .out0(decoder_1_out0), .out1(decoder_1_out1), .out2(decoder_1_out2), .out3(decoder_1_out3),
    .out4(decoder_1_out4), .out5(decoder_1_out5), .out6(decoder_1_out6), .sel(CONDITION[4:0]));  // open: out7, out8, out9, out10, out11, out12, out13, out14, out15, out16, out17, out18, out19, out20, out21, out22, out23, out24, out25, out26, out27, out28, out29, out30, out31
  or or_1 (or_1_out, LT, EQ);
  or or_2 (or_2_out, EQ, GT);
  not not_1 (not_1_out, EQ);
  and and_1 (and_1_out, EQ, decoder_1_out1);
  and and_2 (and_2_out, not_1_out, decoder_1_out2);
  and and_3 (and_3_out, LT, decoder_1_out3);
  and and_4 (and_4_out, GT, decoder_1_out4);
  and and_5 (and_5_out, or_1_out, decoder_1_out5);
  and and_6 (and_6_out, or_2_out, decoder_1_out6);
  or or_3 (CONDITION_MET, decoder_1_out0, and_1_out, and_2_out, and_3_out, and_4_out, and_5_out, and_6_out);
endmodule

module WtB (
  input  [15:0] in_1,
  output [7:0] out_2
);


  assign out_2 = in_1[15:8];
endmodule

module RGBC (
  input  [7:0] in_1,
  input  [7:0] in_2,
  input  [7:0] in_3,
  output [23:0] out_4
);


  assign out_4 = {in_3, in_2, in_1};
endmodule
